# Fritzing sketch not-kiwi-bot (saved by Fritzing 0.9.3b)

parts:
  Raspberry_Pi_1 = Raspberry Pi 3 [part_number=RPI-3-V1.2]
  GP-20U7 = GP-20U7
  PWM1 = PCA9685 16x12-bit PWM Breakout

nets:
  N1: Raspberry_Pi_1.3v3, PWM1.no_name_yet#505
  N2: Raspberry_Pi_1.GPIO2, PWM1.no_name_yet#504
  N3: Raspberry_Pi_1.GPIO3, PWM1.no_name_yet#503
  GND: Raspberry_Pi_1.GND, GP-20U7.GND, PWM1.no_name_yet#501
  N4: Raspberry_Pi_1.GPIO22, GP-20U7.VCC
  N5: Raspberry_Pi_1.GPIO15, GP-20U7.TX
